// Logisim project ALU.circ as structural Verilog: 2 circuits, main circuit ALU_1bit
module ALU_1bit (
  input  S0,
  input  S1,
  input  S2,
  input  C_in,
  input  A,
  input  B,
  output C_out,
  output G
);

  wire arithmetic_unit_1bit_1_g, logicial_unit_1bit_1_result;

  arithmetic_unit_1bit arithmetic_unit_1bit_1 (
    .C_in(C_in), .A(A), .B(B), .S0(S0), .S1(S1), .G(arithmetic_unit_1bit_1_g), .C_out(C_out));
  Logicial_Unit_1bit logicial_unit_1bit_1 (.S0(S0), .S1(S1), .A(A), .B(B), .Result(logicial_unit_1bit_1_result));
  MyMultiplexer mymultiplexer_1 (.S0(S2), .A(arithmetic_unit_1bit_1_g), .B(logicial_unit_1bit_1_result), .Result(G));
endmodule

module ALU_nbit (
  input  S0,
  input  S1,
  input  S2,
  input  C_in,
  input  A0,
  input  A1,
  input  A2,
  input  A3,
  input  B0,
  input  B1,
  input  B2,
  input  B3,
  output C_out,
  output G0,
  output G1,
  output G2,
  output G3
);

  wire arithmetic_unit_nbit_1_g0, arithmetic_unit_nbit_1_g1, arithmetic_unit_nbit_1_g2,
       arithmetic_unit_nbit_1_g3, logical_unit_fourbit_1_r0, logical_unit_fourbit_1_r1,
       logical_unit_fourbit_1_r2, logical_unit_fourbit_1_r3;

  arithmetic_unit_nbit arithmetic_unit_nbit_1 (
    .C_in(C_in), .A0(A0), .A1(A1), .A2(A2), .A3(A3), .B0(B0), .B1(B1), .B2(B2), .B3(B3), .S0(S0), .S1(S1),
    .G0(arithmetic_unit_nbit_1_g0), .G1(arithmetic_unit_nbit_1_g1), .G2(arithmetic_unit_nbit_1_g2),
    .G3(arithmetic_unit_nbit_1_g3), .C_out(C_out));
  Logical_Unit_fourbit logical_unit_fourbit_1 (
    .S0(S0), .S1(S1), .A0(A0), .A1(A1), .A2(A2), .A3(A3), .B0(B0), .B1(B1), .B2(B2), .B3(B3),
    .R0(logical_unit_fourbit_1_r0), .R1(logical_unit_fourbit_1_r1), .R2(logical_unit_fourbit_1_r2),
    .R3(logical_unit_fourbit_1_r3));
  MyMultiplexer mymultiplexer_1 (.S0(S2), .A(arithmetic_unit_nbit_1_g0), .B(logical_unit_fourbit_1_r0), .Result(G0));
  MyMultiplexer mymultiplexer_2 (.S0(S2), .A(arithmetic_unit_nbit_1_g1), .B(logical_unit_fourbit_1_r1), .Result(G1));
  MyMultiplexer mymultiplexer_3 (.S0(S2), .A(arithmetic_unit_nbit_1_g2), .B(logical_unit_fourbit_1_r2), .Result(G2));
  MyMultiplexer mymultiplexer_4 (.S0(S2), .A(arithmetic_unit_nbit_1_g3), .B(logical_unit_fourbit_1_r3), .Result(G3));
endmodule
