// Logisim project Addition.circ as structural Verilog: 3 circuits, main circuit main
module main (
);

  CarryLookAhead carrylookahead_1 ();  // open: A0, A1, A2, A3, Cin, B0, B1, B2, B3, Sum0, Sum1, Sum2, Sum3, Cout
endmodule

module FullAdder (
  input  A,
  input  B,
  input  Cin,
  output out_4,
  output out_5
);

  wire and_1_out, and_2_out, xor_1_out;

  xor xor_1 (xor_1_out, A, B);
  and and_1 (and_1_out, A, B);
  and and_2 (and_2_out, xor_1_out, Cin);
  xor xor_2 (out_4, xor_1_out, Cin);
  or or_1 (out_5, and_1_out, and_2_out);
endmodule

module CarryLookAhead (
  input  A0,
  input  A1,
  input  A2,
  input  A3,
  input  Cin,
  input  B0,
  input  B1,
  input  B2,
  input  B3,
  output Sum0,
  output Sum1,
  output Sum2,
  output Sum3,
  output Cout
);

  wire fulladder_1_out_5, fulladder_2_out_5, fulladder_3_out_5;

  FullAdder fulladder_1 (.A(A0), .B(B0), .Cin(Cin), .out_4(Sum0), .out_5(fulladder_1_out_5));
  FullAdder fulladder_2 (.A(A1), .B(B1), .Cin(fulladder_1_out_5), .out_4(Sum1), .out_5(fulladder_2_out_5));
  FullAdder fulladder_3 (.A(A2), .B(B2), .Cin(fulladder_2_out_5), .out_4(Sum2), .out_5(fulladder_3_out_5));
  FullAdder fulladder_4 (.A(A3), .B(B3), .Cin(fulladder_3_out_5), .out_4(Sum3), .out_5(Cout));
endmodule
