// Logisim project B_input_logic.circ as structural Verilog: 3 circuits, main circuit B_input_logic_1bit
module B_input_logic_1bit (
  input  S0,
  input  S1,
  input  B,
  output Y
);

  wire and_1_out, and_2_out, not_1_out;

  not not_1 (not_1_out, B);
  and and_1 (and_1_out, B, S0);
  and and_2 (and_2_out, not_1_out, S1);
  or or_1 (Y, and_1_out, and_2_out);
endmodule

module B_input_logic_nbit (
  input  S0,
  input  S1,
  input  B0,
  input  B1,
  input  B2,
  input  B3,
  output Y0,
  output Y1,
  output Y2,
  output Y3
);

  B_input_logic_1bit b_input_logic_1bit_1 (.S0(S0), .S1(S1), .B(B0), .Y(Y0));
  B_input_logic_1bit b_input_logic_1bit_2 (.S0(S0), .S1(S1), .B(B1), .Y(Y1));
  B_input_logic_1bit b_input_logic_1bit_3 (.S0(S0), .S1(S1), .B(B2), .Y(Y2));
  B_input_logic_1bit b_input_logic_1bit_4 (.S0(S0), .S1(S1), .B(B3), .Y(Y3));
endmodule

module chronogram (
  output Y
);

  wire and_1_out, and_2_out, B_out, not_1_out, S0_out, S1_out;

  Clock sysclock ();  // open: out
  Clock B (.out(B_out));
  not not_1 (not_1_out, B_out);
  Clock #(.highDuration(4), .lowDuration(2), .phaseOffset(1)) S0 (.out(S0_out));
  Clock #(.highDuration(4), .lowDuration(4), .phaseOffset(2)) S1 (.out(S1_out));
  and and_1 (and_1_out, B_out, S0_out);
  and and_2 (and_2_out, not_1_out, S1_out);
  or or_1 (Y, and_1_out, and_2_out);
endmodule
