// Logisim project Circuit.circ as structural Verilog: 17 circuits, main circuit main
module main (
);

  CarryLookAhead carrylookahead_1 ();  // open: A0, A1, A2, A3, Cin, B0, B1, B2, B3, Sum0, Sum1, Sum2, Sum3, Cout
endmodule

module halfAdder (
  input  A,
  input  B,
  output Sum,
  output Cout
);

  and and_1 (Cout, B, A);
  xor xor_1 (Sum, A, B);
endmodule

module FullAdder (
  input  A,
  input  B,
  input  Cin,
  output Res,
  output Cout
);

  wire and_1_out, and_2_out, xor_1_out;

  xor xor_1 (xor_1_out, A, B);
  and and_1 (and_1_out, A, B);
  and and_2 (and_2_out, xor_1_out, Cin);
  xor xor_2 (Res, xor_1_out, Cin);
  or or_1 (Cout, and_1_out, and_2_out);
endmodule

module CarryLookAhead (
  input  A0,
  input  A1,
  input  A2,
  input  A3,
  input  Cin,
  input  B0,
  input  B1,
  input  B2,
  input  B3,
  output Sum0,
  output Sum1,
  output Sum2,
  output Sum3,
  output Cout
);

  wire fulladder_1_cout, fulladder_2_cout, fulladder_3_cout;

  FullAdder fulladder_1 (.A(A0), .B(B0), .Cin(Cin), .Res(Sum0), .Cout(fulladder_1_cout));
  FullAdder fulladder_2 (.A(A1), .B(B1), .Cin(fulladder_1_cout), .Res(Sum1), .Cout(fulladder_2_cout));
  FullAdder fulladder_3 (.A(A2), .B(B2), .Cin(fulladder_2_cout), .Res(Sum2), .Cout(fulladder_3_cout));
  FullAdder fulladder_4 (.A(A3), .B(B3), .Cin(fulladder_3_cout), .Res(Sum3), .Cout(Cout));
endmodule

module B_input_logic_1bit (
  input  S0,
  input  S1,
  input  B,
  output Y
);

  wire and_1_out, and_2_out, not_1_out;

  not not_1 (not_1_out, B);
  and and_1 (and_1_out, B, S0);
  and and_2 (and_2_out, not_1_out, S1);
  or or_1 (Y, and_1_out, and_2_out);
endmodule

module B_input_logic_nbit (
  input  S0,
  input  S1,
  input  B0,
  input  B1,
  input  B2,
  input  B3,
  output Y0,
  output Y1,
  output Y2,
  output Y3
);

  B_input_logic_1bit b_input_logic_1bit_1 (.S0(S0), .S1(S1), .B(B0), .Y(Y0));
  B_input_logic_1bit b_input_logic_1bit_2 (.S0(S0), .S1(S1), .B(B1), .Y(Y1));
  B_input_logic_1bit b_input_logic_1bit_3 (.S0(S0), .S1(S1), .B(B2), .Y(Y2));
  B_input_logic_1bit b_input_logic_1bit_4 (.S0(S0), .S1(S1), .B(B3), .Y(Y3));
endmodule

module chronogram (
  output Y
);

  wire and_1_out, and_2_out, B_out, not_1_out, S0_out, S1_out;

  Clock sysclock ();  // open: out
  Clock B (.out(B_out));
  not not_1 (not_1_out, B_out);
  Clock #(.highDuration(4), .lowDuration(2), .phaseOffset(1)) S0 (.out(S0_out));
  Clock #(.highDuration(4), .lowDuration(4), .phaseOffset(2)) S1 (.out(S1_out));
  and and_1 (and_1_out, B_out, S0_out);
  and and_2 (and_2_out, not_1_out, S1_out);
  or or_1 (Y, and_1_out, and_2_out);
endmodule

module Logicial_Unit_1bit (
  input  S0,
  input  S1,
  input  A,
  input  B,
  output Result
);

  wire and_1_out, and_2_out, and_3_out, and_4_out, and_5_out, not_1_out, not_2_out, not_3_out, or_1_out,
       xor_1_out;

  and and_1 (and_1_out, A, B);
  or or_1 (or_1_out, A, B);
  xor xor_1 (xor_1_out, A, B);
  not not_1 (not_1_out, A);
  not not_2 (not_2_out, S0);
  not not_3 (not_3_out, S1);
  and and_2 (and_2_out, not_2_out, not_3_out, and_1_out);
  and and_3 (and_3_out, S0, not_3_out, or_1_out);
  and and_4 (and_4_out, not_2_out, S1, xor_1_out);
  and and_5 (and_5_out, S0, S1, not_1_out);
  or or_2 (Result, and_2_out, and_3_out, and_4_out, and_5_out);
endmodule

module Logical_Unit_fourbit (
  input  S0,
  input  S1,
  input  A0,
  input  A1,
  input  A2,
  input  A3,
  input  B0,
  input  B1,
  input  B2,
  input  B3,
  output R0,
  output R1,
  output R2,
  output R3
);

  Logicial_Unit_1bit logicial_unit_1bit_1 (.S0(S0), .S1(S1), .A(A0), .B(B0), .Result(R0));
  Logicial_Unit_1bit logicial_unit_1bit_2 (.S0(S0), .S1(S1), .A(A1), .B(B1), .Result(R1));
  Logicial_Unit_1bit logicial_unit_1bit_3 (.S0(S0), .S1(S1), .A(A2), .B(B2), .Result(R2));
  Logicial_Unit_1bit logicial_unit_1bit_4 (.S0(S0), .S1(S1), .A(A3), .B(B3), .Result(R3));
endmodule

module MyMultiplexer (
  input  S0,
  input  A,
  input  B,
  output Result
);

  wire and_1_out, and_2_out, not_1_out;

  not not_1 (not_1_out, S0);
  and and_1 (and_1_out, A, not_1_out);
  and and_2 (and_2_out, B, S0);
  or or_1 (Result, and_1_out, and_2_out);
endmodule

module Arithmetic_Unit_1bit (
  input  C_in,
  input  A,
  input  B,
  input  S0,
  input  S1,
  output G,
  output C_out
);

  wire b_input_logic_1bit_1_y;

  B_input_logic_1bit b_input_logic_1bit_1 (.S0(S0), .S1(S1), .B(B), .Y(b_input_logic_1bit_1_y));
  FullAdder fulladder_1 (.A(A), .B(b_input_logic_1bit_1_y), .Cin(C_in), .Res(G), .Cout(C_out));
endmodule

module Arithmetic_Unit_4bit (
  input  C_in,
  input  A0,
  input  A1,
  input  A2,
  input  A3,
  input  B0,
  input  B1,
  input  B2,
  input  B3,
  input  S0,
  input  S1,
  output G0,
  output G1,
  output G2,
  output G3,
  output C_out
);

  wire b_input_logic_nbit_1_y0, b_input_logic_nbit_1_y1, b_input_logic_nbit_1_y2, b_input_logic_nbit_1_y3;

  B_input_logic_nbit b_input_logic_nbit_1 (
    .S0(S0), .S1(S1), .B0(B0), .B1(B1), .B2(B2), .B3(B3), .Y0(b_input_logic_nbit_1_y0),
    .Y1(b_input_logic_nbit_1_y1), .Y2(b_input_logic_nbit_1_y2), .Y3(b_input_logic_nbit_1_y3));
  CarryLookAhead carrylookahead_1 (
    .A0(A0), .A1(A1), .A2(A2), .A3(A3), .Cin(C_in), .B0(b_input_logic_nbit_1_y0),
    .B1(b_input_logic_nbit_1_y1), .B2(b_input_logic_nbit_1_y2), .B3(b_input_logic_nbit_1_y3), .Sum0(G0),
    .Sum1(G1), .Sum2(G2), .Sum3(G3), .Cout(C_out));
endmodule

module ALU (
  input  S2,
  input  S0,
  input  S1,
  input  C_in,
  input  A,
  input  B,
  output C_out,
  output G
);

  wire arithmetic_unit_1bit_1_g, logicial_unit_1bit_1_result;

  Arithmetic_Unit_1bit arithmetic_unit_1bit_1 (
    .C_in(C_in), .A(A), .B(B), .S0(S0), .S1(S1), .G(arithmetic_unit_1bit_1_g), .C_out(C_out));
  Logicial_Unit_1bit logicial_unit_1bit_1 (.S0(S0), .S1(S1), .A(A), .B(B), .Result(logicial_unit_1bit_1_result));
  MyMultiplexer mymultiplexer_1 (.S0(S2), .A(arithmetic_unit_1bit_1_g), .B(logicial_unit_1bit_1_result), .Result(G));
endmodule

module ALU_nBit (
  input  S2,
  input  C_in,
  input  A0,
  input  A1,
  input  A2,
  input  A3,
  input  S0,
  input  S1,
  input  B0,
  input  B1,
  input  B2,
  input  B3,
  output C_out,
  output G0,
  output G1,
  output G2,
  output G3
);

  wire arithmetic_unit_4bit_1_g0, arithmetic_unit_4bit_1_g1, arithmetic_unit_4bit_1_g2,
       arithmetic_unit_4bit_1_g3, logical_unit_fourbit_1_r0, logical_unit_fourbit_1_r1,
       logical_unit_fourbit_1_r2, logical_unit_fourbit_1_r3;

  Arithmetic_Unit_4bit arithmetic_unit_4bit_1 (
    .C_in(C_in), .A0(A0), .A1(A1), .A2(A2), .A3(A3), .B0(B0), .B1(B1), .B2(B2), .B3(B3), .S0(S0), .S1(S1),
    .G0(arithmetic_unit_4bit_1_g0), .G1(arithmetic_unit_4bit_1_g1), .G2(arithmetic_unit_4bit_1_g2),
    .G3(arithmetic_unit_4bit_1_g3), .C_out(C_out));
  Logical_Unit_fourbit logical_unit_fourbit_1 (
    .S0(S0), .S1(S1), .A0(A0), .A1(A1), .A2(A2), .A3(A3), .B0(B0), .B1(B1), .B2(B2), .B3(B3),
    .R0(logical_unit_fourbit_1_r0), .R1(logical_unit_fourbit_1_r1), .R2(logical_unit_fourbit_1_r2),
    .R3(logical_unit_fourbit_1_r3));
  MyMultiplexer mymultiplexer_1 (.S0(S2), .A(arithmetic_unit_4bit_1_g0), .B(logical_unit_fourbit_1_r0), .Result(G0));
  MyMultiplexer mymultiplexer_2 (.S0(S2), .A(arithmetic_unit_4bit_1_g1), .B(logical_unit_fourbit_1_r1), .Result(G1));
  MyMultiplexer mymultiplexer_3 (.S0(S2), .A(arithmetic_unit_4bit_1_g2), .B(logical_unit_fourbit_1_r2), .Result(G2));
  MyMultiplexer mymultiplexer_4 (.S0(S2), .A(arithmetic_unit_4bit_1_g3), .B(logical_unit_fourbit_1_r3), .Result(G3));
endmodule

module ex1_5_a (
  input  X,
  input  Y,
  input  Z,
  output F
);

  wire and_1_out, and_2_out, not_1_out, or_1_out;

  not not_1 (not_1_out, X);
  or or_1 (or_1_out, Y, Z);
  and and_1 (and_1_out, X, or_1_out);
  and and_2 (and_2_out, not_1_out, Z);
  or or_2 (F, and_1_out, and_2_out);
endmodule

module ex1_5_created (
  input  X,
  input  Y,
  input  Z,
  output F
);

  wire and_1_out, and_2_out, not_1_out, or_1_out;

  not not_1 (not_1_out, X);
  and and_1 (and_1_out, X, or_1_out);
  or or_1 (or_1_out, Z, Y);
  and and_2 (and_2_out, Z, not_1_out);
  or or_2 (F, and_1_out, and_2_out);
endmodule

module ex1_5_created_optimized (
  input  X,
  input  Y,
  input  Z,
  output F
);

  wire and_1_out;

  or or_1 (F, Z, and_1_out);
  and and_1 (and_1_out, X, Y);
endmodule
