// Logisim project Logicial_Unit_fourbit.circ as structural Verilog: 2 circuits, main circuit Logicial_Unit_1bit
module Logicial_Unit_1bit (
  input  S0,
  input  S1,
  input  A,
  input  B,
  output Result
);

  wire and_1_out, and_2_out, and_3_out, and_4_out, and_5_out, not_1_out, not_2_out, not_3_out, or_1_out,
       xor_1_out;

  and and_1 (and_1_out, A, B);
  or or_1 (or_1_out, A, B);
  xor xor_1 (xor_1_out, A, B);
  not not_1 (not_1_out, A);
  not not_2 (not_2_out, S0);
  not not_3 (not_3_out, S1);
  and and_2 (and_2_out, not_2_out, not_3_out, and_1_out);
  and and_3 (and_3_out, S0, not_3_out, or_1_out);
  and and_4 (and_4_out, not_2_out, S1, xor_1_out);
  and and_5 (and_5_out, S0, S1, not_1_out);
  or or_2 (Result, and_2_out, and_3_out, and_4_out, and_5_out);
endmodule

module Logical_Unit_fourbit (
  input  S0,
  input  S1,
  input  A0,
  input  A1,
  input  A2,
  input  A3,
  input  B0,
  input  B1,
  input  B2,
  input  B3,
  output R0,
  output R1,
  output R2,
  output R3
);

  Logicial_Unit_1bit logicial_unit_1bit_1 (.S0(S0), .S1(S1), .A(A0), .B(B0), .Result(R0));
  Logicial_Unit_1bit logicial_unit_1bit_2 (.S0(S0), .S1(S1), .A(A1), .B(B1), .Result(R1));
  Logicial_Unit_1bit logicial_unit_1bit_3 (.S0(S0), .S1(S1), .A(A2), .B(B2), .Result(R2));
  Logicial_Unit_1bit logicial_unit_1bit_4 (.S0(S0), .S1(S1), .A(A3), .B(B3), .Result(R3));
endmodule
