// Logisim project Logicial_Unit_onebit.circ as structural Verilog: 2 circuits, main circuit main
module main (
  input  S0,
  input  S1,
  input  A1,
  input  in_4,
  input  in_5,
  input  in_6,
  input  in_7,
  input  in_8,
  input  in_9,
  input  in_10
);

  // Logicial_Unit_1bit logicial_unit_1bit_1: pin names not known; wires that end beside it: A1, S0, S1, A1
endmodule

module Logicial_Unit_1bit (
  input  S0,
  input  S1,
  input  A,
  input  B,
  output Result
);

  wire and_1_out, and_2_out, and_3_out, and_4_out, and_5_out, not_1_out, not_2_out, not_3_out, or_1_out,
       xor_1_out;

  and and_1 (and_1_out, A, B);
  or or_1 (or_1_out, A, B);
  xor xor_1 (xor_1_out, A, B);
  not not_1 (not_1_out, A);
  not not_2 (not_2_out, S0);
  not not_3 (not_3_out, S1);
  and and_2 (and_2_out, not_2_out, and_1_out);
  and and_3 (and_3_out, S0, or_1_out);
  and and_4 (and_4_out, not_2_out, xor_1_out);
  and and_5 (and_5_out, S0, not_1_out);
  or or_2 (Result, and_2_out, and_5_out);
endmodule
