// Logisim project DDC_Project_Multiplexer.circ as structural Verilog: 1 circuit, main circuit MyMultiplexer
module MyMultiplexer (
  input  S0,
  input  A,
  input  B,
  output Result
);

  wire and_1_out, and_2_out, not_1_out;

  not not_1 (not_1_out, S0);
  and and_1 (and_1_out, A, not_1_out);
  and and_2 (and_2_out, B, S0);
  or or_1 (Result, and_1_out, and_2_out);
endmodule
