// Logisim project arithmetic_unit.circ as structural Verilog: 2 circuits, main circuit arithmetic_unit_1bit
module arithmetic_unit_1bit (
  input  C_in,
  input  A,
  input  B,
  input  S0,
  input  S1,
  output G,
  output C_out
);

  wire b_input_logic_1bit_1_y;

  B_input_logic_1bit b_input_logic_1bit_1 (.S0(S0), .S1(S1), .B(B), .Y(b_input_logic_1bit_1_y));
  FullAdder fulladder_1 (.A(A), .B(b_input_logic_1bit_1_y), .Cin(C_in), .out_4(G), .out_5(C_out));
endmodule

module arithmetic_unit_nbit (
  input  C_in,
  input  A0,
  input  A1,
  input  A2,
  input  A3,
  input  B0,
  input  B1,
  input  B2,
  input  B3,
  input  S0,
  input  S1,
  output G0,
  output G1,
  output G2,
  output G3,
  output C_out
);

  wire b_input_logic_nbit_1_y0, b_input_logic_nbit_1_y1, b_input_logic_nbit_1_y2, b_input_logic_nbit_1_y3;

  B_input_logic_nbit b_input_logic_nbit_1 (
    .S0(S0), .S1(S1), .B0(B0), .B1(B1), .B2(B2), .B3(B3), .Y0(b_input_logic_nbit_1_y0),
    .Y1(b_input_logic_nbit_1_y1), .Y2(b_input_logic_nbit_1_y2), .Y3(b_input_logic_nbit_1_y3));
  CarryLookAhead carrylookahead_1 (
    .A0(A0), .A1(A1), .A2(A2), .A3(A3), .Cin(C_in), .B0(b_input_logic_nbit_1_y0),
    .B1(b_input_logic_nbit_1_y1), .B2(b_input_logic_nbit_1_y2), .B3(b_input_logic_nbit_1_y3), .Sum0(G0),
    .Sum1(G1), .Sum2(G2), .Sum3(G3), .Cout(C_out));
endmodule
